// Logisim project Projet_base.circ as structural Verilog: 5 circuits, main circuit main
module main (
  output [2:0] opcode,
  output [2:0] ri,
  output [4:0] imm,
  output [7:0] x8
);

  wire clock, CLOCK_out, enableWrite, eq0, IncOrDec, isJMP, isSTP, isZ, not_1_out, reset;
  wire [7:0] alu_1_sortie, PC;

  Button u_CLOCK (.out(CLOCK_out));
  Button u_RESET (.out(reset));
  Controller controller_1 (
    .op(opcode), .isJPM(isJMP), .isZ(isZ), .isSTP(isSTP), .enableWrite(enableWrite), .IncOrDec(IncOrDec));
  assign clock = not_1_out ? CLOCK_out : 1'bz;  // Controlled_Buffer controlled_buffer_1
  not not_1 (not_1_out, isSTP);
  nextAddrLogic nextaddrlogic_1 (
    .Imm5(imm), .isJMP(isJMP), .eq0(eq0), .isZ(isZ), .clock(clock), .reset(reset), .PC(PC));
  regfileV2 regfilev2_1 (
    .value(alu_1_sortie), .enableWrite(enableWrite), .ri(imm[4:2]), .clock(clock), .reset(reset),
    .currRegValue(x8));
  RAM #(.bus("separate")) ram_1 (
    .addr(PC), .data({opcode, imm}), .str(1'b0), .sel(1'b1), .clk(clock), .ld(1'b1), .clr(1'b0));  // open: din
  ALU alu_1 (.\entrée (x8), .IncOrDec(IncOrDec), .sortie(alu_1_sortie), .eq0(eq0));

  assign ri = imm[4:2];

  // Other names for the same wires on the sheet: Imm5[4:0] = imm; op[2:0] = opcode
endmodule

module Controller (
  input  [2:0] op,
  output isJPM,
  output isZ,
  output isSTP,
  output enableWrite,
  output IncOrDec
);

  wire not_1_out, not_2_out, not_3_out;

  not not_1 (not_1_out, op[2]);
  not not_2 (not_2_out, op[0]);
  not not_3 (not_3_out, op[1]);
  and and_1 (isJPM, not_1_out, op[1], not_2_out);
  and and_2 (isZ, not_1_out, op[1], op[0]);
  and and_3 (isSTP, op[2], not_3_out, not_2_out);
  and and_4 (enableWrite, not_1_out, not_3_out);
  and and_5 (IncOrDec, not_1_out, not_3_out, op[0]);
endmodule

module ALU (
  input  IncOrDec,
  input  [7:0] \entrée ,
  output [7:0] sortie,
  output eq0
);

  wire [7:0] adder_1_out, not_1_out, subtractor_1_out;

  assign not_1_out = ~\entrée ;  // NOT_Gate not_1, 8 bits wide
  Adder adder_1 (.a(\entrée ), .b(8'h1), .out(adder_1_out));  // open: cin, cout
  Subtractor subtractor_1 (.a(\entrée ), .b(8'h1), .out(subtractor_1_out));  // open: bin, bout
  Multiplexer #(.width(8), .enable("false")) multiplexer_1 (
    .in0(adder_1_out), .in1(subtractor_1_out), .out(sortie), .sel(IncOrDec));
  and and_1 (eq0, not_1_out[0], not_1_out[1], not_1_out[2], not_1_out[3], not_1_out[4], not_1_out[5], not_1_out[6], not_1_out[7]);
endmodule

module nextAddrLogic (
  input  [4:0] Imm5,
  input  isJMP,
  input  eq0,
  input  clock,
  input  reset,
  input  isZ,
  output [7:0] PC
);

  wire [1:1] and_1_out;
  wire [7:0] adder_1_out, adder_2_out, multiplexer_1_out;

  Adder adder_1 (.a(8'h2), .b(PC), .out(adder_1_out));  // open: cin, cout
  Adder adder_2 (.a(8'h1), .b(PC), .out(adder_2_out));  // open: cin, cout
  and and_1 (and_1_out[1], eq0, isZ);
  Multiplexer #(.select(2), .width(8), .enable("false")) multiplexer_1 (
    .in0(adder_2_out), .in1({3'b000, Imm5}), .in2(adder_1_out), .out(multiplexer_1_out),
    .sel({and_1_out[1], isJMP}));  // open: in3
  Register pcREG (.D(multiplexer_1_out), .en(1'b1), .Q(PC), .clk(clock), .clr(reset));

  // Other names for the same wires on the sheet: reg[7:0] = PC
endmodule

module regfileV2 (
  input  [2:0] ri,
  input  [7:0] value,
  input  enableWrite,
  input  clock,
  input  reset,
  output [7:0] currRegValue
);

  wire e0, e1, e2, e3, e4, e5, e6, e7;
  wire [7:0] s0, s1, s2, s3, s4, s5, s6, s7;

  Demultiplexer #(.select(3), .enable("false")) demultiplexer_1 (
    .out0(e0), .out1(e1), .out2(e2), .out3(e3), .out4(e4), .out5(e5), .out6(e6), .out7(e7), .in(enableWrite),
    .sel(ri));
  Multiplexer #(.select(3), .width(8), .enable("false")) multiplexer_1 (
    .in0(s0), .in1(s1), .in2(s2), .in3(s3), .in4(s4), .in5(s5), .in6(s6), .in7(s7), .out(currRegValue),
    .sel(ri));
  Register _0 (.D(value), .en(e0), .Q(s0), .clk(clock), .clr(reset));
  Register _4 (.D(value), .en(e4), .Q(s4), .clk(clock), .clr(reset));
  Register _1 (.D(value), .en(e1), .Q(s1), .clk(clock), .clr(reset));
  Register _5 (.D(value), .en(e5), .Q(s5), .clk(clock), .clr(reset));
  Register _2 (.D(value), .en(e2), .Q(s2), .clk(clock), .clr(reset));
  Register _6 (.D(value), .en(e6), .Q(s6), .clk(clock), .clr(reset));
  Register _3 (.D(value), .en(e3), .Q(s3), .clk(clock), .clr(reset));
  Register _7 (.D(value), .en(e7), .Q(s7), .clk(clock), .clr(reset));

  // Other names for the same wires on the sheet: clk = clock; enbl = enableWrite; i[2:0] = ri; rst = reset;
  //   val[7:0] = value
endmodule
